# Fritzing sketch SwitchUSB (saved by Fritzing 0.9.3b)
breadboards: 1

parts:
  USB_In = USB Connectors [package=usb-a-s]
  USB_Out_2 = USB Connectors [package=usb-a-h]
  USB_Out_1 = USB Connectors [package=usb-a-h]
  Relay2 = RELAY [package=relay-t9a]
  Relay1 = RELAY [package=relay-t9a]
  Button = Round Pushbutton

nets:
  N1: USB_In.D+, USB_Out_2.D+
  N2: USB_In.D-, Relay2.MAIN
  GND: USB_In.GND, USB_Out_2.GND, USB_Out_1.GND, Relay2.COIL1, Relay1.COIL1
  N3: USB_In.VBUS, Relay1.MAIN
  N4: USB_Out_2.D-, Relay2.NO
  N5: USB_Out_2.VBUS, Relay1.NO
  N6: USB_Out_1.D-, Relay2.NC
  N7: USB_Out_1.D+, Button.leg1
  N8: USB_Out_1.VBUS, Relay1.NC
  N9: Relay2.COIL2, Relay1.COIL2, Button.leg0

notes:
  Switch USB, This project is a switch USB of quickly swapping between devices - https://github.com/gbzarelli/switch-usb, 1
  <HelpDev>
